# Fritzing sketch minno-perf (saved by Fritzing 0.9.3b)
breadboards: 1

parts:
  Part1 = Arduino Leonardo (Rev3b)
  S1 = Toggle Switch [package=THT]
  R3 = Resistor [tolerance=±5% resistance=330k package=THT]
  P1 = S1133 Si Photodiode [package="8mm Ceramic [THT]"]
  R2 = Resistor [tolerance=±5% resistance=10k package="2010 [SMD]"]

nets:
  N1: Part1.D0/RX, Part1.5V, P1.anode, R2.Pin_0
  N2: Part1.D4/A6, S1.L2, R2.Pin_1
  N3: Part1.GND, S1.COM, R3.Pin_0
  N4: R3.Pin_1, P1.cathode
