# Fritzing sketch minno (saved by Fritzing 0.9.3b)
breadboards: 1

parts:
  Part1 = Arduino Leonardo (Rev3b)
  R1 = Resistor [tolerance=±5% resistance=390k package="2010 [SMD]"]
  R2 = Resistor [tolerance=±5% resistance=10k package="2010 [SMD]"]
  P1 = S1133 Si Photodiode [package="8mm Ceramic [THT]"]
  S1 = Toggle Switch [package=THT]

nets:
  N1: Part1.D4/A6, R2.Pin_0, S1.L2
  N2: Part1.5V, P1.cathode, S1.COM
  N3: Part1.GND, R1.Pin_1, R2.Pin_1
  N4: Part1.A0, R1.Pin_0, P1.anode
